# Fritzing sketch Tlacitko (saved by Fritzing 0.9.3b)
breadboards: 1

parts:
  LED1 = LED - 5mm [color="Red (633nm)" package="5 mm [THT]"]
  LED2 = LED - 5mm [color="Orange (620nm)" package="5 mm [THT]"]
  LED3 = LED - 5mm [color="Green (570nm)" package="5 mm [THT]"]
  LED4 = LED - 5mm [color="Red (633nm)" package="5 mm [THT]"]
  LED5 = LED - 5mm [color="Orange (620nm)" package="5 mm [THT]"]
  LED6 = LED - 5mm [color="Green (570nm)" package="5 mm [THT]"]
  LED7 = LED - 5mm [color="Green (565nm)" package="5 mm [THT]"]
  LED8 = LED - 5mm [color="Red (633nm)" package="5 mm [THT]"]
  R1 = Resistor [tolerance=±5% resistance=220 package=THT]
  R2 = Resistor [tolerance=±5% resistance=220 package=THT]
  R3 = Resistor [tolerance=±5% resistance=220 package=THT]
  R4 = Resistor [tolerance=±5% resistance=220 package=THT]
  R5 = Resistor [tolerance=±5% resistance=220 package=THT]
  R6 = Resistor [tolerance=±5% resistance=220 package=THT]
  R7 = Resistor [tolerance=±5% resistance=220 package=THT]
  R8 = Resistor [tolerance=±5% resistance=220 package=THT]
  Součástka1 = Arduino Uno (Rev3)
  S1 = Pushbutton [package="[THT]"]
  S2 = Pushbutton [package="[THT]"]
  R9 = Resistor [tolerance=±5% resistance=220 package=THT]
  R10 = Resistor [tolerance=±5% resistance=220 package=THT]

nets:
  N1: LED1.cathode, R2.Pin_0
  N2: LED1.anode, Součástka1.D13/SCK
  N3: LED2.cathode, R1.Pin_1
  N4: LED2.anode, Součástka1.D12/MISO
  N5: LED3.cathode, R3.Pin_1
  N6: LED3.anode, Součástka1.D11_PWM/MOSI
  N7: LED4.cathode, R6.Pin_1
  N8: LED4.anode, Součástka1.D8
  N9: LED5.cathode, R7.Pin_1
  N10: LED5.anode, Součástka1.D7
  N11: LED6.cathode, R8.Pin_1
  N12: LED6.anode, Součástka1.D6_PWM
  N13: LED7.cathode, R4.Pin_1
  N14: LED7.anode, Součástka1.D10_PWM/SS
  N15: LED8.cathode, R5.Pin_1
  N16: LED8.anode, Součástka1.D9_PWM
  N17: R1.Pin_0, R2.Pin_1, R3.Pin_0, R4.Pin_0, R5.Pin_0, R6.Pin_0, R7.Pin_0, R8.Pin_0, Součástka1.GND, R9.Pin_0, R10.Pin_0
  N18: Součástka1.D4, S2.Pin_1, S2.Pin_2, R10.Pin_1
  N19: Součástka1.D5_PWM, S1.Pin_3, S1.Pin_4, R9.Pin_1
  N20: Součástka1.5V, S1.Pin_1, S1.Pin_2, S2.Pin_3, S2.Pin_4

// code stored in the sketch: Tlacitko.ino

int LED1 = 9;	// nastavení pinu na ke kterému je p?ipojena LED
int Tlacitko = 2;// nastavení pinu na kterém je p?ipojeno tla?ítko 

void setup(){
	pinMode(LED1,OUTPUT); // nastavení pinu LED1  jako výstpní
	pinMode(Tlacitko,INPUT); // nastavení pinu Tlaciko jako  vstupní
}
void loop(){
	if(digitalRead(Tlacitko) == 1) // pokud je na pin Tlaciko p?ivedeno 5V ( tlacitko je  zmá?knuto) tak rozsvi? LED
		digitalWrite(LED1,1); // nastaví výstup pinu LED1 na 1 (5V)
	else
		digitalWrite(LED1,0); // nastaví výstup LED1 na 0 (0V)
	
}
