# Fritzing sketch semafor (saved by Fritzing 0.9.3b)
breadboards: 1

parts:
  LED1 = LED - 5mm [color="Red (633nm)" package="5 mm [THT]"]
  LED2 = LED - 5mm [color="Orange (620nm)" package="5 mm [THT]"]
  LED3 = LED - 5mm [color="Green (570nm)" package="5 mm [THT]"]
  LED4 = LED - 5mm [color="Red (633nm)" package="5 mm [THT]"]
  LED5 = LED - 5mm [color="Orange (620nm)" package="5 mm [THT]"]
  LED6 = LED - 5mm [color="Green (570nm)" package="5 mm [THT]"]
  LED7 = LED - 5mm [color="Green (565nm)" package="5 mm [THT]"]
  LED8 = LED - 5mm [color="Red (633nm)" package="5 mm [THT]"]
  R1 = Resistor [tolerance=±5% resistance=220 package=THT]
  R2 = Resistor [tolerance=±5% resistance=220 package=THT]
  R3 = Resistor [tolerance=±5% resistance=220 package=THT]
  R4 = Resistor [tolerance=±5% resistance=220 package=THT]
  R5 = Resistor [tolerance=±5% resistance=220 package=THT]
  R6 = Resistor [tolerance=±5% resistance=220 package=THT]
  R7 = Resistor [tolerance=±5% resistance=220 package=THT]
  R8 = Resistor [tolerance=±5% resistance=220 package=THT]
  Součástka1 = Arduino Uno (Rev3)
  S1 = Pushbutton [package="[THT]"]
  S2 = Pushbutton [package="[THT]"]
  R9 = Resistor [tolerance=±5% resistance=220 package=THT]
  R10 = Resistor [tolerance=±5% resistance=220 package=THT]

nets:
  N1: LED1.cathode, R2.Pin_0
  N2: LED1.anode, Součástka1.D13/SCK
  N3: LED2.cathode, R1.Pin_1
  N4: LED2.anode, Součástka1.D12/MISO
  N5: LED3.cathode, R3.Pin_1
  N6: LED3.anode, Součástka1.D11_PWM/MOSI
  N7: LED4.cathode, R6.Pin_1
  N8: LED4.anode, Součástka1.D8
  N9: LED5.cathode, R7.Pin_1
  N10: LED5.anode, Součástka1.D7
  N11: LED6.cathode, R8.Pin_1
  N12: LED6.anode, Součástka1.D6_PWM
  N13: LED7.cathode, R4.Pin_1
  N14: LED7.anode, Součástka1.D10_PWM/SS
  N15: LED8.cathode, R5.Pin_1
  N16: LED8.anode, Součástka1.D9_PWM
  N17: R1.Pin_0, R2.Pin_1, R3.Pin_0, R4.Pin_0, R5.Pin_0, R6.Pin_0, R7.Pin_0, R8.Pin_0, Součástka1.GND, R9.Pin_0, R10.Pin_0
  N18: Součástka1.D4, S2.Pin_1, S2.Pin_2, R10.Pin_1
  N19: Součástka1.D5_PWM, S1.Pin_3, S1.Pin_4, R9.Pin_1
  N20: Součástka1.5V, S1.Pin_1, S1.Pin_2, S2.Pin_3, S2.Pin_4

// code stored in the sketch: Semafor.ino
int Semafor1[] = { 11,12,13};
int Semafor_Chodci[] = {10,9};
int Semafor3[] = {6,7,8};


int aktivni_semafor = 0;


int tlacitko1 = 4 ;
int tlacitko2 =  5;


long interval = 10000;
long cas = 0;


void RozsvitZelenou(int semafor[]){
    digitalWrite(semafor[2],1);
    digitalWrite(semafor[1],1);
    digitalWrite(semafor[2],0);
    delay(1000);
    digitalWrite(semafor[2],0);
    digitalWrite(semafor[1],0);
    digitalWrite(semafor[0],1);
}
void RozsvitCervenou(int semafor[]){
    digitalWrite(semafor[2],0);
    digitalWrite(semafor[1],1);
    digitalWrite(semafor[0],0);
    delay(1000);
    digitalWrite(semafor[2],1);
    digitalWrite(semafor[1],0);
    digitalWrite(semafor[0],0);
}
void ChodciZelena(int Semafor[]){
    digitalWrite(Semafor[1],0);
    digitalWrite(Semafor[0],1);
}
void ChodciCervena(int Semafor[]){
    digitalWrite(Semafor[1],1);
    digitalWrite(Semafor[0],0);
}



void setup(){
    for(int i = 6; i < 14; i++)
        pinMode(i ,OUTPUT);
    pinMode(4,OUTPUT);
    pinMode(5,OUTPUT);
}
void loop(){
    if(digitalRead(tlacitko1) == 1 || digitalRead(tlacitko2) == 1){
        if(aktivni_semafor == 1){
            RozsvitCervenou(Semafor1);   
        }
        else{
            RozsvitCervenou(Semafor3);
        }
        delay(1000);
        ChodciZelena(Semafor_Chodci);
        delay(5000);
        ChodciCervena(Semafor_Chodci);
    }
    if(cas - millis() > interval){
        if(aktivni_semafor == 1){ 
            aktivni_semafor = 2;
            RozsvitCervenou(Semafor1);
            RozsvitZelenou(Semafor3);
        }
        else{
            aktivni_semafor = 1;
            RozsvitCervenou(Semafor3);
            RozsvitZelenou(Semafor1);
        }
        cas = millis();
    }
        
}
